# Fritzing sketch Fritzing Sketch (saved by Fritzing 0.8.7b)
breadboards: 1

parts:
  Part1 = Arduino Uno (Rev3)
  KEYPAD1 = Membrane Matrix Keypad
  U1 = LCD-16X2 [package=lcd-16x2_noholes]
  LED1 = LED - 5mm [color="Red (633nm)" package="5 mm [THT]"]
  LED2 = LED - 5mm [color="Green (555nm)" package="5 mm [THT]"]
  R1 = Resistor [tolerance=±5% resistance=330 package=THT]
  R2 = Resistor [tolerance=±5% resistance=330 package=THT]
  J1 = Piezo Speaker
  J2 = Screw terminal - 2 pins [package=THT]

nets:
  N1: Part1.A0, Part1.A1, Part1.A2, Part1.A3, Part1.GND, U1.K, R1.Pin_1, R2.Pin_1, J1.pin1, J2.pin2
  N2: Part1.A4/SDA, U1.VSS
  N3: Part1.A5/SCL, U1.VDD
  N4: Part1.D8, KEYPAD1.2
  N5: Part1.D9_PWM, KEYPAD1.1
  N6: Part1.D10_PWM/SS, LED1.cathode
  N7: Part1.D11_PWM/MOSI, J2.pin1
  N8: Part1.D12/MISO, J1.pin2
  N9: Part1.D3_PWM, KEYPAD1.7
  N10: Part1.D4, KEYPAD1.6
  N11: Part1.D5_PWM, KEYPAD1.5
  N12: Part1.D6_PWM, KEYPAD1.4
  N13: Part1.D7, KEYPAD1.3
  N14: Part1.5V, U1.A, LED2.cathode
  N15: LED1.anode, R1.Pin_0
  N16: LED2.anode, R2.Pin_0

notes:
  I've used I2C version of the screen which only uses 2 IOs.
  Wiring shown here isn't correct.
  My project uses 4x4 matrix, but unfortunately, such model is not available in Fritzing
  Wires comming from IOs A0 - A3 are used for manual defuse
  IO D11 is used for initiator, initiator must be present in order to arm the bomb.
  Initiator is just a resistor that shorts D11 to ground.

custom parts:
  Membrane Matrix Keypad: Membrane Matrix 3x4 Keypad
